# Fritzing sketch knob_sketch (saved by Fritzing 0.9.2b)

parts:
  Part1 = Arduino Micro (Rev3)
  RE1 = Rotary Encoder [package=THT]

nets:
  N1: Part1.GND, RE1.EncoderPinC
  N2: Part1.D2/SDA, RE1.EncoderPinB
  N3: Part1.D3/SCL, RE1.EncoderPinA
