# Fritzing sketch zoombox (saved by Fritzing 0.9.4)

parts:
  Part2 = Arduino Micro (Rev3)
  S1 = Round Pushbutton
  S2 = Round Pushbutton
  S3 = Round Pushbutton
  U1 = SWITCH_SPDT [package=kps-1290]
  S4 = Pushbutton [package="[THT]"]
  S5 = Pushbutton [package="[THT]"]
  S6 = Pushbutton [package="[THT]"]
  S7 = Pushbutton [package="[THT]"]
  S8 = Pushbutton [package="[THT]"]
  S9 = Pushbutton [package="[THT]"]

nets:
  N1: Part2.GND, S1.leg1
  N2: Part2.D3/SCL, S8.Pin_4
  N3: Part2.D4_PWM/A6, S5.Pin_3, S5.Pin_4, S6.Pin_1, S6.Pin_2
  N4: Part2.D5_PWM, S6.Pin_4
  N5: Part2.D6_PWM/A7, S7.Pin_4
  N6: Part2.D7, S9.Pin_4
  N7: Part2.D8_PWM/A8, S4.Pin_4
  N8: Part2.D9_PWM/A9, U1.P
  N9: Part2.D10_PWM/A10, S3.leg0
  N10: Part2.D11_PWM, S2.leg0
  N11: Part2.D12_PWM/A11, S1.leg0
  N12: Part2.3V3, U1.O
